// Logisim project 3_iny_priklad.circ as structural Verilog: 1 circuit, main circuit main
module main (
  input  a,
  input  b,
  output out_3,
  output out_4,
  output out_5
);

  wire clock_1_out, d_ff_1_qn, d_ff_2_qn, nand_1_out, nand_2_out, nand_3_out, nand_4_out, nand_5_out,
       nand_6_out, nand_7_out, nand_8_out, nand_9_out, not_1_out, not_2_out;

  not not_1 (not_1_out, a);
  not not_2 (not_2_out, b);
  nand nand_1 (nand_1_out, not_2_out, out_3);
  nand nand_2 (nand_2_out, a, not_2_out);
  nand nand_3 (nand_3_out, out_3, a);
  nand nand_4 (nand_4_out, out_5, not_1_out);
  nand nand_5 (nand_5_out, not_1_out, b);
  nand nand_6 (nand_6_out, out_5, b);
  Clock clock_1 (.out(clock_1_out));
  nand nand_7 (nand_7_out, nand_1_out, nand_2_out, nand_3_out);
  nand nand_8 (nand_8_out, nand_4_out, nand_5_out, nand_6_out);
  D_Flip_Flop d_ff_1 (.clk(clock_1_out), .D(nand_7_out), .Q(out_3), .Qn(d_ff_1_qn));  // open: preset, en, reset
  D_Flip_Flop d_ff_2 (.clk(clock_1_out), .D(nand_8_out), .Q(out_5), .Qn(d_ff_2_qn));  // open: preset, en, reset
  nand nand_9 (nand_9_out, d_ff_1_qn, d_ff_2_qn);
  nand nand_10 (out_4, nand_9_out, nand_9_out);
endmodule
