// Logisim project main.circ as structural Verilog: 1 circuit, main circuit main
module main (
  input  X,
  input  Res,
  output Y
);

  wire clock_1_out, nand_1_out, nX_out, X_____Z1___Z3_out, X_____Z3___X___Z2___Z3_out, X_____Z3_out,
       X____Z3_______X____Z3_out, X____Z3_out, X___Z2___Z3___X___Z2___Z3_out, X___Z2___Z3_out,
       Z1____X______Z3______X_____Z3_out, Z1____X______Z3_____Z1___Z3_out, Z1____X______Z3_out, Z1___Z3_out,
       Z1_q, Z2____Z3______X_out, Z2_q, Z3_2_q, Z3_out;

  nand nX (nX_out, X, X);
  nand X_____Z1___Z3 (X_____Z1___Z3_out, Z1_q, Z3_2_q, nX_out);
  nand X_____Z1___Z3____X_____Z1___Z3 (Y, X_____Z1___Z3_out, X_____Z1___Z3_out);
  nand X___Z2___Z3 (X___Z2___Z3_out, X, Z2_q, Z3_2_q);
  nand Z3 (Z3_out, Z3_2_q, Z3_2_q);
  nand X_____Z3 (X_____Z3_out, nX_out, Z3_2_q, Z3_2_q);
  nand Z1____X______Z3 (Z1____X______Z3_out, Z1_q, nX_out, Z3_out);
  nand Z1___Z3 (Z1___Z3_out, Z1_q, Z3_2_q);
  nand Z2____Z3______X (Z2____Z3______X_out, Z3_out, nX_out, Z2_q);
  nand X____Z3 (X____Z3_out, Z3_out, X);
  Clock clock_1 (.out(clock_1_out));
  nand X___Z2___Z3___X___Z2___Z3 (X___Z2___Z3___X___Z2___Z3_out, X___Z2___Z3_out, X___Z2___Z3_out);
  nand Z1____X______Z3_____Z1___Z3 (Z1____X______Z3_____Z1___Z3_out, Z1____X______Z3_out, Z1___Z3_out);
  nand Z1____X______Z3______X_____Z3 (Z1____X______Z3______X_____Z3_out, Z1____X______Z3_out, X_____Z3_out);
  nand nand_1 (nand_1_out, X___Z2___Z3_out, Z2____Z3______X_out);
  nand X____Z3_______X____Z3 (X____Z3_______X____Z3_out, X____Z3_out, X____Z3_out);
  nand X_____Z3___X___Z2___Z3 (X_____Z3___X___Z2___Z3_out, X_____Z3_out, X___Z2___Z3_out);
  J_K_Flip_Flop Z1 (
    .J(X___Z2___Z3___X___Z2___Z3_out), .clk(clock_1_out), .K(Z1____X______Z3_____Z1___Z3_out), .Q(Z1_q),
    .reset(Res));  // open: Qn, preset, en
  J_K_Flip_Flop Z2 (
    .J(Z1____X______Z3______X_____Z3_out), .clk(clock_1_out), .K(nand_1_out), .Q(Z2_q), .reset(Res));  // open: Qn, preset, en
  J_K_Flip_Flop Z3_2 (
    .J(X____Z3_______X____Z3_out), .clk(clock_1_out), .K(X_____Z3___X___Z2___Z3_out), .Q(Z3_2_q), .reset(Res));  // open: Qn, preset, en
endmodule
